# Fritzing sketch Computer Controller (saved by Fritzing 0.9.3b)
circuit board: 8.46667cm x 5.64444cm

parts:
  Q1 = NPN-Transistor [package="TO92 [THT]"]
  Q2 = NPN-Transistor [package="TO92 [THT]"]
  Q3 = NPN-Transistor [package="TO92 [THT]"]
  Q4 = NPN-Transistor [package="TO92 [THT]"]  # not connected
  R1 = Resistor [tolerance=±5% resistance=12k package=THT]
  R2 = Resistor [tolerance=±5% resistance=12k package=THT]
  R3 = Resistor [tolerance=±5% resistance=12k package=THT]
  R4 = Resistor [tolerance=±5% resistance=1k package=THT]
  R5 = Resistor [tolerance=±5% resistance=10k package=THT]

nets:
  N1: Q1.B, R3.Pin_0
  N2: Q2.B, R1.Pin_0
  N3: Q3.E, R4.Pin_0
  N4: Q3.B, R2.Pin_0
  GND: Q3.C
  N5: R4.Pin_1, R5.Pin_0
  3.3V: R5.Pin_1
