# Fritzing sketch Untitled Sketch 2 (saved by Fritzing 0.9.3b)
circuit board: 8.46667cm x 5.64444cm

parts:
  U1 = NodeMCU V1.0
  Digispark1 = Digispark
  Password_entry = NPN-Transistor [package="TO92 [THT]"]
  PC_power = NPN-Transistor [package="TO92 [THT]"]
  PC_reset = NPN-Transistor [package="TO92 [THT]"]
  PC_Input = NPN-Transistor [package="TO92 [THT]"]

nets:
  N1: U1.3V3, PC_Input.E
  GND: U1.GND, Digispark1.GND, Password_entry.E
  N2: U1.D6, PC_power.B
  N3: U1.D7, PC_reset.B
  N4: U1.D8, PC_Input.C
  VIN: U1.Vin, Digispark1.VCC
  N5: Digispark1.P0, Password_entry.C

custom parts:
  NodeMCU V1.0: ESP8266 based NodeMCU
  Digispark: The Digispark is an Attiny85 based microcontroller development board similar to the Arduino line, only cheaper, smaller, and a bit less powerful. With a whole host of shields to extend its functionality and the ability to use the familiar Arduino IDE the Digispark is a great way to jump into electronics, or perfect for when an Arduino is too big or too much.
